// Logisim project ALU.circ as structural Verilog: 1 circuit, main circuit ALU
module ALU (
  input  [31:0] A,
  input  [31:0] B,
  input  [2:0] F,
  output out_4,
  output [31:0] out_5
);

  wire comparator_2_lt;
  wire [31:0] ADD, AND, OR, sll, SLT, SUB;

  Shifter #(.width(32)) shifter_1 (.in(B), .\dist (A[4:0]), .out(sll));
  Multiplexer #(.select(3), .width(32)) multiplexer_1 (
    .in0(AND), .in1(OR), .in2(ADD), .in3({32{1'b0}}), .in4({32{1'b0}}), .in5(sll), .in6(SUB), .in7(SLT),
    .out(out_5), .sel(F));  // open: en
  Comparator #(.width(32)) comparator_1 (.a(A), .b(B), .eq(out_4));  // open: gt, lt
  Adder #(.width(32)) adder_1 (.a(A), .b(B), .out(ADD));  // open: cin, cout
  Subtractor #(.width(32)) subtractor_1 (.a(A), .b(B), .out(SUB));  // open: bin, bout
  Comparator #(.width(32)) comparator_2 (.a(A), .b(B), .lt(comparator_2_lt));  // open: gt, eq
  assign SLT = {{31{1'b0}}, comparator_2_lt};  // Bit_Extender bit_extender_1
  assign AND = A & B;  // AND_Gate and_1, 32 bits wide
  assign OR = A | B;  // OR_Gate or_1, 32 bits wide

  // Other names for the same wires on the sheet: Y[31:0] = out_5; Zero = out_4

  // Notes on the sheet:
  //   ILAM UNI-Spring 2017
  //   Arithmetic Logic Unit (ALU)
endmodule
