// Logisim project Control.circ as structural Verilog: 1 circuit, main circuit main
module main (
  input  [5:0] opCode,
  input  eq,
  input  [2:0] funct,
  output ALUSrc,
  output JUMP,
  output memToReg,
  output memWrite,
  output regDST,
  output regWrite,
  output branch,
  output Sing,
  output [2:0] ALUCtr
);

  wire add_out, addi_out, addu_out, and_out, andi_out, beq_out, or_5_out, or_out, ori_out, slt_out, sltu_out,
       sub_out, subu_out;
  wire [2:0] multiplexer_1_out, multiplexer_2_out, multiplexer_3_out, multiplexer_4_out, multiplexer_5_out,
       multiplexer_6_out, multiplexer_7_out, multiplexer_8_out, multiplexer_9_out, multiplexer_10_out;

  and R_Type (regDST, ~opCode[5], ~opCode[4], ~opCode[3], ~opCode[2], ~opCode[1], ~opCode[0]);  // AND_Gate
  and add (add_out, ~funct[2], ~funct[1], ~funct[0], regDST);  // AND_Gate
  and addi (addi_out, ~opCode[5], ~opCode[4], opCode[3], ~opCode[2], ~opCode[1], ~opCode[0]);  // AND_Gate
  and \or  (or_out, ~funct[2], ~funct[1], funct[0], regDST);  // AND_Gate
  Multiplexer #(.width(3)) multiplexer_1 (
    .in0(3'b000), .in1(3'b001), .out(multiplexer_1_out), .sel(or_out));  // open: en
  Multiplexer #(.width(3)) multiplexer_2 (
    .in0(3'b000), .in1(3'b010), .out(multiplexer_2_out), .sel(add_out));  // open: en
  and andi (andi_out, ~opCode[5], ~opCode[4], opCode[3], opCode[2], ~opCode[1], ~opCode[0]);  // AND_Gate
  and addu (addu_out, ~funct[2], funct[1], ~funct[0], regDST);  // AND_Gate
  Multiplexer #(.width(3)) multiplexer_3 (
    .in0(3'b000), .in1(3'b010), .out(multiplexer_3_out), .sel(addu_out));  // open: en
  and beq (beq_out, ~opCode[5], ~opCode[4], ~opCode[3], opCode[2], ~opCode[1], ~opCode[0]);  // AND_Gate
  and slt (slt_out, funct[2], ~funct[1], ~funct[0], regDST);  // AND_Gate
  and subu (subu_out, ~funct[2], funct[1], funct[0], regDST);  // AND_Gate
  Multiplexer #(.width(3)) multiplexer_4 (
    .in0(3'b000), .in1(3'b110), .out(multiplexer_4_out), .sel(subu_out));  // open: en
  and j (JUMP, ~opCode[5], ~opCode[4], ~opCode[3], ~opCode[2], opCode[1], ~opCode[0]);  // AND_Gate
  and sub (sub_out, funct[2], ~funct[1], funct[0], regDST);  // AND_Gate
  Multiplexer #(.width(3)) multiplexer_5 (
    .in0(3'b000), .in1(3'b110), .out(multiplexer_5_out), .sel(sub_out));  // open: en
  Multiplexer #(.width(3)) multiplexer_6 (
    .in0(3'b000), .in1(3'b111), .out(multiplexer_6_out), .sel(slt_out));  // open: en
  and lw (memToReg, opCode[5], ~opCode[4], ~opCode[3], ~opCode[2], opCode[1], opCode[0]);  // AND_Gate
  and sltu (sltu_out, funct[2], funct[1], ~funct[0], regDST);  // AND_Gate
  Multiplexer #(.width(3)) multiplexer_7 (
    .in0(3'b000), .in1(3'b111), .out(multiplexer_7_out), .sel(sltu_out));  // open: en
  and ori (ori_out, ~opCode[5], ~opCode[4], opCode[3], opCode[2], ~opCode[1], opCode[0]);  // AND_Gate
  and \and  (and_out, funct[2], funct[1], funct[0], regDST);
  and sw (memWrite, opCode[5], ~opCode[4], opCode[3], ~opCode[2], opCode[1], opCode[0]);  // AND_Gate
  Multiplexer #(.width(3)) multiplexer_8 (
    .in0(3'b000), .in1(3'b000), .out(multiplexer_8_out), .sel(and_out));  // open: en
  Multiplexer #(.width(3)) multiplexer_9 (
    .in0(3'b000), .in1(3'b010), .out(multiplexer_9_out), .sel(addi_out));  // open: en
  or or_2 (ALUSrc, memWrite, ori_out, andi_out, addi_out);
  or or_3 (regWrite, ori_out, memToReg, andi_out, addi_out, regDST);
  and and_2 (branch, beq_out, eq);
  or or_4 (Sing, memWrite, memToReg, addi_out, andi_out);
  or or_5 (or_5_out, andi_out, beq_out, memToReg, memWrite, ori_out);
  Multiplexer #(.width(3)) multiplexer_10 (
    .in0(3'b000), .in1(3'b101), .out(multiplexer_10_out), .sel(or_5_out));  // open: en
  assign ALUCtr = multiplexer_9_out | multiplexer_8_out | multiplexer_7_out | multiplexer_6_out | multiplexer_5_out | multiplexer_4_out | multiplexer_3_out | multiplexer_1_out | multiplexer_2_out | multiplexer_10_out;  // OR_Gate or_6, 3 bits wide
endmodule
