// Logisim project INSTURCTION.circ as structural Verilog: 1 circuit, main circuit main
module main (
  input  [31:0] Fetch_Address,
  input  CLK,
  input  in_3,
  input  in_4,
  output [15:0] out_5,
  output [2:0] FUNCT,
  output [7:0] out_7,
  output [4:0] RD,
  output [4:0] RT,
  output [4:0] RS,
  output [5:0] out_11,
  output [27:0] out_12
);

  wire or_1_out;
  wire [27:0] bit_extender_1_out;
  wire [31:0] multiplexer_1_out, rom_1_data;

  or or_1 (or_1_out, in_4, in_3);
  Multiplexer #(.width(32)) multiplexer_1 (
    .in0(rom_1_data), .in1({32{1'b0}}), .out(multiplexer_1_out), .sel(or_1_out));  // open: en
  Register #(.width(32)) register_1 (
    .D(multiplexer_1_out), .Q({out_11, RS, RT, out_5[15:3], FUNCT}), .clk(CLK));  // open: en, clr
  ROM #(.addrWidth(24), .dataWidth(32)) rom_1 (.addr(Fetch_Address[25:2]), .data(rom_1_data));  // open: sel
  assign bit_extender_1_out = {{2{1'b0}}, {RS, RT, out_5[15:3], FUNCT}};  // Bit_Extender bit_extender_1
  Shifter #(.width(28)) shifter_1 (.in(bit_extender_1_out), .\dist (5'b00010), .out(out_12));

  assign out_5[2:0] = FUNCT;
  assign out_7 = out_5[10:3];
  assign RD = out_5[15:11];

  // Notes on the sheet:
  //   BRANCH
  //   JUMP
  //   Instruction Memory
  //   imm
  //   Unused
  //   OP CODE
  //   ADDRESS
endmodule
