// Logisim project PC.circ as structural Verilog: 1 circuit, main circuit main
module main (
  input  [31:0] Fetch_Address,
  input  [15:0] imm,
  input  branch,
  input  jump,
  input  CLK,
  input  [27:0] in_6,
  output [31:0] Fetch_Address_2
);

  wire [31:0] adder_2_out, bit_extender_1_out, multiplexer_1_out, multiplexer_2_out, PC___4, shifter_1_out;

  Adder #(.width(32)) adder_1 (.a(Fetch_Address), .b(32'h4), .out(PC___4));  // open: cin, cout
  assign bit_extender_1_out = {{16{imm[15]}}, imm};  // Bit_Extender bit_extender_1
  Shifter #(.width(32)) shifter_1 (.in(bit_extender_1_out), .\dist (5'b00010), .out(shifter_1_out));
  Adder #(.width(32)) adder_2 (.a(PC___4), .b(shifter_1_out), .out(adder_2_out));  // open: cin, cout
  Multiplexer #(.width(32)) multiplexer_1 (
    .in0(PC___4), .in1(adder_2_out), .out(multiplexer_1_out), .sel(branch));  // open: en
  Multiplexer #(.width(32)) multiplexer_2 (
    .in0(multiplexer_1_out), .in1({PC___4[31:28], in_6}), .out(multiplexer_2_out), .sel(jump));  // open: en
  Register #(.width(32)) PC (.D(multiplexer_2_out), .Q(Fetch_Address_2), .clk(CLK));  // open: en, clr

  // Notes on the sheet:
  //   ADDRESS
  //   PC+4
endmodule
