// Logisim project cpu.circ as structural Verilog: 1 circuit, main circuit main
// sing
module main (
);

  wire ALUSrc, branch, clk, equal, jump, memToReg, memWrite, regDST, regWrite, sing;
  wire [2:0] ALUCtr, funct;
  wire [3:0] adder_1_out_2;
  wire [4:0] multiplexer_3_out, rd, rs, rt;
  wire [5:0] opcode;
  wire [15:0] immediate;
  wire [27:0] adder_1_out, address;
  wire [31:0] adder_2_out, alu_1_out_5, bit_extender_1_out, bit_extender_2_out, main_3_read_data_1,
       main_3_read_data_2, main_4_p5, multiplexer_1_out, multiplexer_2_out, multiplexer_4_out,
       multiplexer_5_out, PC_q, shifter_1_out, WriteBack;

  Multiplexer #(.width(32)) multiplexer_1 (
    .in0({adder_1_out_2, adder_1_out}), .in1(adder_2_out), .out(multiplexer_1_out), .sel(branch));  // open: en
  Multiplexer #(.width(32)) multiplexer_2 (
    .in0(multiplexer_1_out), .in1({adder_1_out_2, address}), .out(multiplexer_2_out), .sel(jump));  // open: en
  Clock clock_1 (.out(clk));
  Register #(.width(32)) PC (.D(multiplexer_2_out), .Q(PC_q), .clk(clk));  // open: en, clr
  Adder #(.width(32)) adder_1 (.a(PC_q), .b(32'h4), .out({adder_1_out_2, adder_1_out}));  // open: cin, cout
  INSTURCTION_main main_1 (
    .Fetch_Address(PC_q), .in_3(jump), .in_4(branch), .out_5(immediate), .FUNCT(funct), .RD(rd), .RT(rt),
    .RS(rs), .out_11(opcode), .out_12(address), .CLK(clk));  // open: out_7
  Control_main main_2 (
    .opCode(opcode), .eq(equal), .funct(funct), .ALUSrc(ALUSrc), .JUMP(jump), .memToReg(memToReg),
    .memWrite(memWrite), .regDST(regDST), .regWrite(regWrite), .branch(branch), .Sing(sing), .ALUCtr(ALUCtr));
  Multiplexer #(.width(5)) multiplexer_3 (.in0(rt), .in1(rd), .out(multiplexer_3_out), .sel(regDST));  // open: en
  regfile_main main_3 (
    .Read_Register_1(rs[2:0]), .Read_Register_2(rt[2:0]), .Write_Register(multiplexer_3_out[2:0]),
    .Write_Data(WriteBack), .Write_Enable(regWrite), .Clock(clk), .Read_Data_1(main_3_read_data_1),
    .Read_Data_2(main_3_read_data_2));
  assign bit_extender_1_out = {{16{1'b0}}, immediate};  // Bit_Extender bit_extender_1
  Multiplexer #(.width(32)) multiplexer_4 (
    .in0(bit_extender_1_out), .in1(bit_extender_2_out), .out(multiplexer_4_out), .sel(sing));  // open: en
  assign bit_extender_2_out = {{16{immediate[15]}}, immediate};  // Bit_Extender bit_extender_2
  Multiplexer #(.width(32)) multiplexer_5 (
    .in0(main_3_read_data_2), .in1(multiplexer_4_out), .out(multiplexer_5_out), .sel(ALUSrc));  // open: en
  Shifter #(.width(32)) shifter_1 (.in(bit_extender_2_out), .\dist (5'b00010), .out(shifter_1_out));
  ALU alu_1 (.A(main_3_read_data_1), .B(multiplexer_5_out), .F(ALUCtr), .out_4(equal), .out_5(alu_1_out_5));
  Adder #(.width(32)) adder_2 (
    .a(shifter_1_out), .b({adder_1_out_2, adder_1_out}), .out(adder_2_out));  // open: cin, cout
  // mem_main main_4: pin names not known; wires that end beside it: alu_1_out_5, main_3_read_data_2, memWrite, clk, main_4_p5, main_4_p5
  Multiplexer #(.width(32)) multiplexer_6 (
    .in0(alu_1_out_5), .in1(main_4_p5), .out(WriteBack), .sel(memToReg));  // open: en

  // Notes on the sheet:
  //   PC+4
  //   32 BIT SINGLE CYCLE CPU
endmodule
