// Logisim project regfile.circ as structural Verilog: 1 circuit, main circuit main
module main (
  input  [2:0] Read_Register_1,
  input  [2:0] Read_Register_2,
  input  [2:0] Write_Register,
  input  [31:0] Write_Data,
  input  Write_Enable,
  input  Clock,
  output [31:0] Read_Data_1,
  output [31:0] Read_Data_2
);

  wire reg1_we, reg2_we, reg3_we, reg4_we, reg5_we, reg6_we, reg7_we;
  wire [31:0] reg0_out, reg1_in, reg1_out, reg2_in, reg2_out, reg3_in, reg3_out, reg4_in, reg4_out, reg5_in,
       reg5_out, reg6_in, reg6_out, reg7_in, reg7_out;

  Demultiplexer #(.select(3)) demultiplexer_1 (
    .out1(reg1_we), .out2(reg2_we), .out3(reg3_we), .out4(reg4_we), .out5(reg5_we), .out6(reg6_we),
    .out7(reg7_we), .in(1'b1), .sel(Write_Register), .en(Write_Enable));  // open: out0
  Multiplexer #(.select(3), .width(32)) multiplexer_1 (
    .in0(reg0_out), .in1(reg1_out), .in2(reg2_out), .in3(reg3_out), .in4(reg4_out), .in5(reg5_out),
    .in6(reg6_out), .in7(reg7_out), .out(Read_Data_1), .sel(Read_Register_1));  // open: en
  Demultiplexer #(.select(3), .width(32)) demultiplexer_2 (
    .out1(reg1_in), .out2(reg2_in), .out3(reg3_in), .out4(reg4_in), .out5(reg5_in), .out6(reg6_in),
    .out7(reg7_in), .in(Write_Data), .sel(Write_Register), .en(Write_Enable));  // open: out0
  Register #(.width(32)) register_1 (.D({32{1'b0}}), .Q(reg0_out));  // open: en, clk, clr
  Register #(.width(32)) register_2 (.D(reg1_in), .en(reg1_we), .Q(reg1_out), .clk(Clock));  // open: clr
  Register #(.width(32)) register_3 (.D(reg2_in), .en(reg2_we), .Q(reg2_out), .clk(Clock));  // open: clr
  Register #(.width(32)) register_4 (.D(reg3_in), .en(reg3_we), .Q(reg3_out), .clk(Clock));  // open: clr
  Register #(.width(32)) register_5 (.D(reg4_in), .en(reg4_we), .Q(reg4_out), .clk(Clock));  // open: clr
  Register #(.width(32)) register_6 (.D(reg5_in), .en(reg5_we), .Q(reg5_out), .clk(Clock));  // open: clr
  Register #(.width(32)) register_7 (.D(reg6_in), .en(reg6_we), .Q(reg6_out), .clk(Clock));  // open: clr
  Register #(.width(32)) register_8 (.D(reg7_in), .en(reg7_we), .Q(reg7_out), .clk(Clock));  // open: clr
  Multiplexer #(.select(3), .width(32)) multiplexer_2 (
    .in0(reg0_out), .in1(reg1_out), .in2(reg2_out), .in3(reg3_out), .in4(reg4_out), .in5(reg5_out),
    .in6(reg6_out), .in7(reg7_out), .out(Read_Data_2), .sel(Read_Register_2));  // open: en

  // Other names for the same wires on the sheet: clk = Clock; read_data1[31:0] = Read_Data_1;
  //   read_data2[31:0] = Read_Data_2; read_reg1[2:0] = Read_Register_1; read_reg2[2:0] = Read_Register_2;
  //   write_en = Write_Enable; write_reg[2:0] = Write_Register

  // Notes on the sheet:
  //   Register File
  //   ILAM UNI-SPRING 2017
endmodule
